# Fritzing sketch sketch (saved by Fritzing 0.9.3b)
breadboards: 1

parts:
  MOTOR1 = 28BYJ-48 Stepper Motor  # not connected
  MOTOR2 = 28BYJ-48 Stepper Motor  # not connected
  BREAKOUT2 = ULN2003A breakout board
  Part1 = Arduino Nano (Rev3.0) (ICSP)
  M1 = fc-51 [package=THT]
  M2 = fc-51 [package=THT]
  M3 = fc-51 [package=THT]
  M4 = fc-51 [package=THT]
  M5 = fc-51 [package=THT]
  U1 = Voltage Regulator - 5V [package="DPak [SMD]"]
  U2 = LIPO-1000mAh [package=lipo-1000]
  BREAKOUT1 = ULN2003A breakout board

nets:
  N1: BREAKOUT2.In_1, Part1.D6
  N2: BREAKOUT2.In_2, Part1.D7
  N3: BREAKOUT2.In_3, Part1.D8
  N4: BREAKOUT2.In_4, Part1.D9
  N5: BREAKOUT2.0V, Part1.GND, M1.pin2, M2.pin2, M3.pin2, M4.pin2, M5.pin2, BREAKOUT1.0V
  +5V: BREAKOUT2.+5V, U1.input_voltage, U2.+, BREAKOUT1.+5V
  N6: Part1.D2, BREAKOUT1.In_1
  N7: Part1.D3, BREAKOUT1.In_2
  N8: Part1.D4, BREAKOUT1.In_3
  N9: Part1.D5, BREAKOUT1.In_4
  N10: Part1.VIN, M1.pin3, M2.pin3, M3.pin3, M4.pin3, M5.pin3, U1.output_voltage
  N11: Part1.A4, M1.pin1
  N12: Part1.A3, M4.pin1
  N13: Part1.A2, M3.pin1
  N14: Part1.A1, M2.pin1
  N15: Part1.A0, M5.pin1
  N16: U1.GND, U2.-

notes:
  l7805cv

custom parts:
  ULN2003A breakout board: ULN2003A 7-way Darlington Transistor Driver on breakoutboard
