# Fritzing sketch sketch (saved by Fritzing 0.9.3b)
breadboards: 1

parts:
  Part3 = 24 NeoPixel Ring [part_number=1586]
  VCC1 = 4 x AAA Battery Mount
  Part5 = Adafruit APDS-9960 [part_number="Adafruit #3595"]
  Part6 = Arduino Uno (Rev3)

nets:
  N1: Part3.IN, Part6.D6_PWM
  VIN: Part3.VDD, VCC1.+, Part5.VIN, Part6.VIN
  GND: Part3.GND, VCC1.-, Part5.GND, Part6.GND
  N2: Part5.SCL, Part6.A5/SCL
  N3: Part5.SDA, Part6.A4/SDA
  N4: Part5.INT, Part6.D2

custom parts:
  24 NeoPixel Ring: 24 ultra bright smart LED NeoPixels are arranged in a circle with 2.6" (66mm) outer diameter. The rings are 'chainable' - connect the output pin of one to the input pin of another. Use only one microcontroller pin to control as many as you can chain together! Each LED is addressable as the driver chip is inside the LED. Each one has ~18mA constant current drive so the color will be very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
  Adafruit APDS-9960: The APDS9960 from Avago Technologies has an integrated IR LED and driver, along with four directional photodiodes that sense reflected IR energy from the LED. It's proximity detection feature allows it to measure the distance an object is from the front of the sensor (up to a few centimeters) with 8 bit resolution. Since there are four IR sensors, you can measure the changes in light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
