# Fritzing sketch sketch (saved by Fritzing 0.9.3b)
breadboards: 1

parts:
  Part3 = 24 NeoPixel Ring [part_number=1586]
  Part4 = Arduino Pro Mini (3.3V)
  VCC1 = 4 x AAA Battery Mount
  GY1 = MPU-6050 Board GY-521 [form="♀ (female)" package=THT]

nets:
  N1: Part3.IN, Part4.D6
  N2: Part3.VDD, Part4.RAW, VCC1.+, GY1.pin1
  GND: Part3.GND, Part4.GND, VCC1.-, GY1.pin2
  N3: Part4.A4, GY1.pin4
  N4: Part4.A5, GY1.pin3

custom parts:
  24 NeoPixel Ring: 24 ultra bright smart LED NeoPixels are arranged in a circle with 2.6" (66mm) outer diameter. The rings are 'chainable' - connect the output pin of one to the input pin of another. Use only one microcontroller pin to control as many as you can chain together! Each LED is addressable as the driver chip is inside the LED. Each one has ~18mA constant current drive so the color will be very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
  MPU-6050 Board GY-521: Acelerometro y Giroscopio MPU-6050 Board GY-521
