# Fritzing sketch sketch (saved by Fritzing 0.9.3b)
breadboards: 1

parts:
  Part4 = Arduino Pro Mini (3.3V)
  VCC1 = 4 x AAA Battery Mount
  Part5 = Bluetooth HC-05 Macho
  Part6 = InvenSense MPU6050

nets:
  GND: Part4.GND, VCC1.-, Part5.GND, Part6.GND
  N1: Part4.A4, Part6.SDA
  N2: Part4.A5, Part6.SCL
  VCC: Part4.RAW, VCC1.+, Part5.VCC, Part6.VCC
  N3: Part4.MOSI, Part5.TXD
  N4: Part4.D10, Part5.RXD
